// Logisim project CMPC.circ as structural Verilog: 11 circuits, main circuit main
module main (
);

  wire alu_1_zero, and_1_out, CLK_out, control_1_branch, control_1_branchcomparator, control_1_byte,
       control_1_fetch, control_1_immflag, control_1_jump, control_1_link, control_1_memread,
       control_1_memwrite, control_1_regwrite, RESET_out, xnor_1_out;
  wire [3:0] multiplexer_3_out, multiplexer_4_out, multiplexer_5_out, regdecoder_1_reg1, regdecoder_1_reg2,
       regdecoder_1_regdest;
  wire [4:0] control_1_aluop;
  wire [7:0] bitselector_4_out;
  wire [15:0] bitselector_3_out;
  wire [23:0] adder_1_out, adder_2_out, bitselector_1_out, bitselector_2_out, multiplexer_1_out,
       multiplexer_2_out, multiplexer_7_out, PC_q;
  wire [25:0] bit_extender_3_out, bitselector_5_out, multiplexer_10_out, shifter_1_out;
  wire [31:0] alu_1_out, bit_extender_1_out, bit_extender_2_out, byteram_1_output, IR_q, multiplexer_6_out,
       multiplexer_8_out, multiplexer_9_out, registers_1_reg1val, registers_1_reg2val;

  and and_1 (and_1_out, control_1_branch, xnor_1_out);
  Multiplexer #(.width(24), .enable("false")) multiplexer_1 (
    .in0(multiplexer_2_out), .in1(adder_2_out), .out(multiplexer_1_out), .sel(and_1_out));
  Button RESET (.out(RESET_out));
  Multiplexer #(.width(24), .enable("false")) multiplexer_2 (
    .in0(multiplexer_7_out), .in1(bitselector_1_out), .out(multiplexer_2_out), .sel(control_1_jump));
  Multiplexer #(.width(4), .enable("false")) multiplexer_3 (
    .in0(regdecoder_1_reg2), .in1(regdecoder_1_regdest), .out(multiplexer_3_out), .sel(control_1_memwrite));
  Register #(.width(24)) PC (.D(multiplexer_1_out), .Q(PC_q), .clk(CLK_out), .clr(RESET_out));  // open: en
  xnor xnor_1 (xnor_1_out, control_1_branchcomparator, alu_1_zero);
  BitSelector #(.width(32), .group(24)) bitselector_1 (.in(registers_1_reg1val), .out(bitselector_1_out), .sel(1'b0));
  Multiplexer #(.width(4), .enable("false")) multiplexer_4 (
    .in0(regdecoder_1_reg1), .in1(regdecoder_1_regdest), .out(multiplexer_4_out), .sel(control_1_jump));
  Multiplexer #(.width(4), .enable("false")) multiplexer_5 (
    .in0(regdecoder_1_regdest), .in1(regdecoder_1_reg1), .out(multiplexer_5_out), .sel(control_1_link));
  Clock CLK (.out(CLK_out));
  Multiplexer #(.width(32), .enable("false")) multiplexer_6 (
    .in0(multiplexer_9_out), .in1(bit_extender_1_out), .out(multiplexer_6_out), .sel(control_1_link));
  regDecoder regdecoder_1 (
    .instruction(IR_q), .regDest(regdecoder_1_regdest), .reg2(regdecoder_1_reg2), .reg1(regdecoder_1_reg1));
  Registers registers_1 (
    .reg1(multiplexer_4_out), .reg1Val(registers_1_reg1val), .Clock(CLK_out), .Data(multiplexer_6_out),
    .WriteFlag(control_1_regwrite), .reg2(multiplexer_3_out), .reg2Val(registers_1_reg2val),
    .DestReg(multiplexer_5_out));
  BitSelector #(.width(32), .group(24)) bitselector_2 (.in(bit_extender_2_out), .out(bitselector_2_out), .sel(1'b0));
  Adder #(.width(24)) adder_1 (.a(PC_q), .b(24'h1), .out(adder_1_out));  // open: cin, cout
  // Probe on multiplexer_9_out
  Adder #(.width(24)) adder_2 (.a(bitselector_2_out), .b(PC_q), .out(adder_2_out));  // open: cin, cout
  Multiplexer #(.width(24), .enable("false")) multiplexer_7 (
    .in0(adder_1_out), .in1(PC_q), .out(multiplexer_7_out), .sel(control_1_fetch));
  Register #(.width(32)) IR (.D(byteram_1_output), .en(control_1_fetch), .Q(IR_q), .clk(CLK_out));  // open: clr
  Multiplexer #(.width(32), .enable("false")) multiplexer_8 (
    .in0(registers_1_reg2val), .in1(bit_extender_2_out), .out(multiplexer_8_out), .sel(control_1_immflag));
  assign bit_extender_1_out = {{8{1'b0}}, adder_1_out};  // Bit_Extender bit_extender_1
  assign bit_extender_2_out = {{16{1'b0}}, bitselector_3_out};  // Bit_Extender bit_extender_2
  BitSelector #(.width(32), .group(16)) bitselector_3 (.in(IR_q), .out(bitselector_3_out), .sel(1'b0));
  BitSelector #(.width(32), .group(8)) bitselector_4 (.in(IR_q), .out(bitselector_4_out), .sel(2'b11));
  ALU alu_1 (
    .op(control_1_aluop), .a(registers_1_reg1val), .b(multiplexer_8_out), .out(alu_1_out), .zero(alu_1_zero));  // open: cbit
  Multiplexer #(.width(32), .enable("false")) multiplexer_9 (
    .in0(alu_1_out), .in1(byteram_1_output), .out(multiplexer_9_out), .sel(control_1_memread));
  control control_1 (
    .opcode(bitselector_4_out), .ALUop(control_1_aluop), .jump(control_1_jump), .\byte (control_1_byte),
    .memread(control_1_memread), .memwrite(control_1_memwrite), .regwrite(control_1_regwrite),
    .immflag(control_1_immflag), .branch(control_1_branch), .branchcomparator(control_1_branchcomparator),
    .fetch(control_1_fetch), .clk(CLK_out), .link(control_1_link));
  assign bit_extender_3_out = {{2{1'b0}}, PC_q};  // Bit_Extender bit_extender_3
  Shifter #(.width(26)) shifter_1 (.in(bit_extender_3_out), .\dist (5'b00010), .out(shifter_1_out));
  BitSelector #(.width(32), .group(26)) bitselector_5 (.in(alu_1_out), .out(bitselector_5_out), .sel(1'b0));
  // Probe on registers_1_reg2val
  Multiplexer #(.width(26), .enable("false")) multiplexer_10 (
    .in0(bitselector_5_out), .in1(shifter_1_out), .out(multiplexer_10_out), .sel(control_1_fetch));
  // Probe on byteram_1_output
  byteRam byteram_1 (
    .mode_0_byte_1_word(control_1_byte), .D(registers_1_reg2val), .A(multiplexer_10_out),
    .store(control_1_memwrite), .Clock(CLK_out), .\output (byteram_1_output));
endmodule

module ALU (
  input  [4:0] op,
  input  [31:0] a,
  input  [31:0] b,
  output [31:0] out,
  output cbit,
  output zero
);

  wire and_1_out, and_2_out, bitselector_4_out, not_2_out;
  wire [1:0] alumuxdec_1_y0;
  wire [4:0] bitselector_1_out, multiplexer_2_out;
  wire [15:0] bitselector_2_out, bitselector_3_out, divider_1_out, divider_1_rem, multiplier_1_cout,
       multiplier_1_out;
  wire [31:0] adder_1_out, and_3_out, bit_extender_1_out, multiplexer_1_out, multiplexer_3_out,
       multiplexer_4_out, not_1_out, not_3_out, or_1_out, shifter_1_out, shifter_2_out, shifter_3_out,
       xor_1_out;

  and and_1 (and_1_out, op[1], op[0]);
  assign not_1_out = ~b;  // NOT_Gate not_1, 32 bits wide
  BitSelector #(.width(32), .group(5)) bitselector_1 (.in(b), .out(bitselector_1_out), .sel(3'b000));
  not not_2 (not_2_out, op[1]);
  and and_2 (and_2_out, op[0], not_2_out);
  Multiplexer #(.width(32), .enable("false")) multiplexer_1 (
    .in0(b), .in1(not_1_out), .out(multiplexer_1_out), .sel(and_2_out));
  Multiplexer #(.width(5), .enable("false")) multiplexer_2 (
    .in0(bitselector_1_out), .in1(5'b10000), .out(multiplexer_2_out), .sel(and_1_out));
  BitSelector #(.width(32), .group(16)) bitselector_2 (.in(a), .out(bitselector_2_out), .sel(1'b0));
  BitSelector #(.width(32), .group(16)) bitselector_3 (.in(b), .out(bitselector_3_out), .sel(1'b0));
  Multiplexer #(.width(32), .enable("false")) multiplexer_3 (
    .in0(a), .in1(b), .out(multiplexer_3_out), .sel(and_1_out));
  ALUmuxDec alumuxdec_1 (
    .B0(op[0]), .B1(op[1]), .B2(op[2]), .B4(op[4]), .Y0(alumuxdec_1_y0[0]), .Y1(alumuxdec_1_y0[1]));
  assign or_1_out = a | multiplexer_1_out;  // OR_Gate or_1, 32 bits wide
  assign and_3_out = a & multiplexer_1_out;  // AND_Gate and_3, 32 bits wide
  assign xor_1_out = a ^ multiplexer_1_out;  // XOR_Gate xor_1, 32 bits wide
  Adder #(.width(32)) adder_1 (.a(a), .b(multiplexer_1_out), .out(adder_1_out), .cin(and_2_out), .cout(cbit));
  Shifter #(.width(32)) shifter_1 (.in(multiplexer_3_out), .\dist (multiplexer_2_out), .out(shifter_1_out));
  Shifter #(.width(32), .shift("lr")) shifter_2 (
    .in(multiplexer_3_out), .\dist (multiplexer_2_out), .out(shifter_2_out));
  Shifter #(.width(32), .shift("ar")) shifter_3 (
    .in(multiplexer_3_out), .\dist (multiplexer_2_out), .out(shifter_3_out));
  BitSelector #(.width(32)) bitselector_4 (.in(adder_1_out), .out(bitselector_4_out), .sel({5{1'b1}}));
  assign bit_extender_1_out = {{31{1'b0}}, bitselector_4_out};  // Bit_Extender bit_extender_1
  Multiplier #(.width(16)) multiplier_1 (
    .a(bitselector_2_out), .b(bitselector_3_out), .out(multiplier_1_out), .cout(multiplier_1_cout));  // open: cin
  Divider #(.width(16)) divider_1 (
    .a(bitselector_2_out), .b(bitselector_3_out), .out(divider_1_out), .rem(divider_1_rem));  // open: upper
  Multiplexer #(.select(3), .width(32), .enable("false")) multiplexer_4 (
    .in0(or_1_out), .in1(and_3_out), .in2(xor_1_out), .in3(adder_1_out), .in4(shifter_1_out),
    .in5(shifter_2_out), .in6(shifter_3_out), .in7(bit_extender_1_out), .out(multiplexer_4_out), .sel(op[4:2]));
  assign not_3_out = ~multiplexer_4_out;  // NOT_Gate not_3, 32 bits wide
  zerocheck zerocheck_1 (.\input (adder_1_out), .zeroflag(zero));
  Multiplexer #(.select(2), .width(32), .enable("false")) multiplexer_5 (
    .in0(multiplexer_4_out), .in1(not_3_out), .in2({multiplier_1_cout, multiplier_1_out}),
    .in3({divider_1_rem, divider_1_out}), .out(out), .sel(alumuxdec_1_y0));
endmodule

// registers
module Registers (
  input  Clock,
  input  [3:0] DestReg,
  input  WriteFlag,
  input  [31:0] Data,
  input  [3:0] reg1,
  input  [3:0] reg2,
  output [31:0] reg1Val,
  output [31:0] reg2Val
);

  wire and_1_out, and_2_out, and_3_out, and_4_out, and_5_out, and_6_out, and_7_out, and_8_out, and_9_out,
       and_10_out, and_11_out, and_12_out, and_13_out, and_14_out, and_15_out, and_16_out, decoder_1_out0,
       decoder_1_out1, decoder_1_out2, decoder_1_out3, decoder_1_out4, decoder_1_out5, decoder_1_out6,
       decoder_1_out7, decoder_1_out8, decoder_1_out9, decoder_1_out10, decoder_1_out11, decoder_1_out12,
       decoder_1_out13, decoder_1_out14, decoder_1_out15;
  wire [31:0] register_1_q, register_2_q, register_3_q, register_4_q, register_5_q, register_6_q,
       register_7_q, register_8_q, register_9_q, register_10_q, register_11_q, register_12_q, register_13_q,
       register_14_q, register_15_q, register_16_q;

  Decoder #(.select(4), .enable("false")) decoder_1 (
    .out0(decoder_1_out0), .out1(decoder_1_out1), .out2(decoder_1_out2), .out3(decoder_1_out3),
    .out4(decoder_1_out4), .out5(decoder_1_out5), .out6(decoder_1_out6), .out7(decoder_1_out7),
    .out8(decoder_1_out8), .out9(decoder_1_out9), .out10(decoder_1_out10), .out11(decoder_1_out11),
    .out12(decoder_1_out12), .out13(decoder_1_out13), .out14(decoder_1_out14), .out15(decoder_1_out15),
    .sel(DestReg));
  and and_1 (and_1_out, decoder_1_out8, WriteFlag);
  and and_2 (and_2_out, decoder_1_out9, WriteFlag);
  and and_3 (and_3_out, decoder_1_out10, WriteFlag);
  and and_4 (and_4_out, decoder_1_out12, WriteFlag);
  and and_5 (and_5_out, decoder_1_out0, WriteFlag);
  and and_6 (and_6_out, decoder_1_out1, WriteFlag);
  and and_7 (and_7_out, decoder_1_out2, WriteFlag);
  and and_8 (and_8_out, decoder_1_out3, WriteFlag);
  and and_9 (and_9_out, decoder_1_out4, WriteFlag);
  and and_10 (and_10_out, decoder_1_out5, WriteFlag);
  and and_11 (and_11_out, decoder_1_out6, WriteFlag);
  and and_12 (and_12_out, decoder_1_out7, WriteFlag);
  and and_13 (and_13_out, decoder_1_out11, WriteFlag);
  and and_14 (and_14_out, decoder_1_out13, WriteFlag);
  and and_15 (and_15_out, decoder_1_out14, WriteFlag);
  and and_16 (and_16_out, decoder_1_out15, WriteFlag);
  Register #(.width(32)) register_1 (.D(Data), .en(and_5_out), .Q(register_1_q), .clk(Clock));  // open: clr
  Register #(.width(32)) register_2 (.D(Data), .en(and_6_out), .Q(register_2_q), .clk(Clock));  // open: clr
  Register #(.width(32)) register_3 (.D(Data), .en(and_7_out), .Q(register_3_q), .clk(Clock));  // open: clr
  Register #(.width(32)) register_4 (.D(Data), .en(and_8_out), .Q(register_4_q), .clk(Clock));  // open: clr
  Register #(.width(32)) register_5 (.D(Data), .en(and_9_out), .Q(register_5_q), .clk(Clock));  // open: clr
  Register #(.width(32)) register_6 (.D(Data), .en(and_10_out), .Q(register_6_q), .clk(Clock));  // open: clr
  Register #(.width(32)) register_7 (.D(Data), .en(and_11_out), .Q(register_7_q), .clk(Clock));  // open: clr
  Register #(.width(32)) register_8 (.D(Data), .en(and_12_out), .Q(register_8_q), .clk(Clock));  // open: clr
  Register #(.width(32)) register_9 (.D(Data), .en(and_1_out), .Q(register_9_q), .clk(Clock));  // open: clr
  Register #(.width(32)) register_10 (.D(Data), .en(and_2_out), .Q(register_10_q), .clk(Clock));  // open: clr
  Register #(.width(32)) register_11 (.D(Data), .en(and_3_out), .Q(register_11_q), .clk(Clock));  // open: clr
  Register #(.width(32)) register_12 (.D(Data), .en(and_13_out), .Q(register_12_q), .clk(Clock));  // open: clr
  Register #(.width(32)) register_13 (.D(Data), .en(and_4_out), .Q(register_13_q), .clk(Clock));  // open: clr
  Register #(.width(32)) register_14 (.D(Data), .en(and_14_out), .Q(register_14_q), .clk(Clock));  // open: clr
  Register #(.width(32)) register_15 (.D(Data), .en(and_15_out), .Q(register_15_q), .clk(Clock));  // open: clr
  Register #(.width(32)) register_16 (.D(Data), .en(and_16_out), .Q(register_16_q), .clk(Clock));  // open: clr
  Multiplexer #(.select(4), .width(32), .enable("false")) multiplexer_1 (
    .in0(register_1_q), .in1(register_2_q), .in2(register_3_q), .in3(register_4_q), .in4(register_5_q),
    .in5(register_6_q), .in6(register_7_q), .in7(register_8_q), .in8(register_9_q), .in9(register_10_q),
    .in10(register_11_q), .in11(register_12_q), .in12(register_13_q), .in13(register_14_q),
    .in14(register_15_q), .in15(register_16_q), .out(reg2Val), .sel(reg2));
  Multiplexer #(.select(4), .width(32), .enable("false")) multiplexer_2 (
    .in0(register_1_q), .in1(register_2_q), .in2(register_3_q), .in3(register_4_q), .in4(register_5_q),
    .in5(register_6_q), .in6(register_7_q), .in7(register_8_q), .in8(register_9_q), .in9(register_10_q),
    .in10(register_11_q), .in11(register_12_q), .in12(register_13_q), .in13(register_14_q),
    .in14(register_15_q), .in15(register_16_q), .out(reg1Val), .sel(reg1));
endmodule

module zerocheck (
  input  [31:0] \input ,
  output zeroflag
);

  nor nor_1 (zeroflag, \input [0], \input [1], \input [2], \input [3], \input [4], \input [5], \input [6], \input [7], \input [8], \input [9], \input [10], \input [11], \input [12], \input [13], \input [14], \input [15], \input [16], \input [17], \input [18], \input [19], \input [20], \input [21], \input [22], \input [23], \input [24], \input [25], \input [26], \input [27], \input [28], \input [29], \input [30], \input [31]);
endmodule

module control (
  input  [7:0] opcode,
  input  clk,
  output [4:0] ALUop,
  output jump,
  output \byte ,
  output memread,
  output memwrite,
  output regwrite,
  output immflag,
  output branch,
  output branchcomparator,
  output link,
  output fetch
);

  wire not_1_out, subcontroller_1_byte, subcontroller_1_memwrite, subcontroller_1_regwrite;

  ALUtranslator alutranslator_1 (
    .a(opcode[3]), .b(opcode[2]), .c(opcode[1]), .d(opcode[0]), .A_2(ALUop[4]), .B_2(ALUop[3]),
    .C_2(ALUop[2]), .D_2(ALUop[1]), .E(ALUop[0]));
  D_Flip_Flop d_ff_1 (.clk(clk), .D(fetch), .Qn(fetch));  // open: Q, preset, en, reset
  subcontroller subcontroller_1 (
    .a(opcode[7]), .b(opcode[6]), .c(opcode[5]), .d(opcode[4]), .jump(jump), .link(link),
    .\byte (subcontroller_1_byte), .memread(memread), .memwrite(subcontroller_1_memwrite),
    .regWrite(subcontroller_1_regwrite), .immflag(immflag), .branch(branch),
    .branchcomparator(branchcomparator));
  or or_1 (\byte , subcontroller_1_byte, fetch);
  not not_1 (not_1_out, fetch);
  and and_1 (regwrite, subcontroller_1_regwrite, not_1_out);
  and and_2 (memwrite, subcontroller_1_memwrite, not_1_out);
endmodule

module ALUtranslator (
  input  a,
  input  b,
  input  c,
  input  d,
  output A_2,
  output B_2,
  output C_2,
  output D_2,
  output E
);

  wire and_1_out, and_2_out, and_3_out, and_4_out, and_5_out, and_6_out, and_7_out, and_8_out, and_9_out,
       and_10_out, and_11_out, and_12_out, and_13_out, and_14_out, and_15_out, and_16_out, and_17_out,
       and_18_out, and_19_out, not_1_out, not_2_out, not_3_out, not_4_out, not_5_out, not_6_out, not_7_out,
       not_8_out, not_9_out, not_10_out, not_11_out, not_12_out, not_13_out, not_14_out, not_15_out,
       not_16_out, not_17_out, not_18_out, not_19_out, not_20_out, not_21_out, not_22_out, not_23_out,
       not_24_out;

  and and_1 (and_1_out, b, c, d);
  not not_1 (not_1_out, b);
  and and_2 (and_2_out, a, not_1_out, not_2_out);
  not not_2 (not_2_out, c);
  not not_3 (not_3_out, b);
  and and_3 (and_3_out, a, not_3_out, not_4_out);
  not not_4 (not_4_out, d);
  not not_5 (not_5_out, c);
  and and_4 (and_4_out, a, not_5_out, not_6_out);
  not not_6 (not_6_out, d);
  not not_7 (not_7_out, a);
  not not_8 (not_8_out, d);
  not not_9 (not_9_out, b);
  not not_10 (not_10_out, d);
  not not_11 (not_11_out, a);
  not not_12 (not_12_out, c);
  not not_13 (not_13_out, b);
  not not_14 (not_14_out, a);
  and and_5 (and_5_out, not_14_out, not_15_out, d);
  not not_15 (not_15_out, c);
  not not_16 (not_16_out, a);
  and and_6 (and_6_out, not_16_out, b, not_17_out);
  not not_17 (not_17_out, d);
  and and_7 (and_7_out, a, not_18_out, not_19_out);
  not not_18 (not_18_out, b);
  not not_19 (not_19_out, d);
  and and_8 (and_8_out, a, b, c);
  not not_20 (not_20_out, b);
  and and_9 (and_9_out, not_20_out, c, d);
  and and_10 (and_10_out, b, not_21_out, not_22_out);
  not not_21 (not_21_out, c);
  not not_22 (not_22_out, d);
  and and_11 (and_11_out, a, b);
  and and_12 (and_12_out, b, c, not_23_out);
  not not_23 (not_23_out, d);
  and and_13 (and_13_out, a, c, not_24_out);
  not not_24 (not_24_out, d);
  and and_14 (and_14_out, a, b);
  or or_1 (A_2, and_1_out, and_2_out, and_3_out, and_4_out);
  and and_15 (and_15_out, not_7_out, c, not_8_out);
  and and_16 (and_16_out, not_9_out, c, not_10_out);
  and and_17 (and_17_out, not_11_out, b, not_12_out, d);
  and and_18 (and_18_out, a, not_13_out, d);
  and and_19 (and_19_out, a, c, d);
  or or_2 (C_2, and_5_out, and_6_out, and_7_out, and_8_out);
  or or_3 (D_2, and_9_out, and_10_out, and_11_out);
  or or_4 (E, and_12_out, and_13_out, and_14_out);
  or or_5 (B_2, and_15_out, and_16_out, and_17_out, and_18_out, and_19_out);
endmodule

module testing (
  input  [1:0] in_1,
  input  [3:0] in_2,
  input  in_3,
  input  [1:0] in_4,
  input  in_5,
  input  [31:0] in_6,
  input  [7:0] in_7,
  input  [7:0] in_8,
  input  [7:0] in_9,
  input  [7:0] in_10,
  input  [25:0] in_11,
  input  [7:0] in_12,
  input  in_13,
  input  in_14,
  input  [7:0] in_15,
  input  [7:0] in_16,
  input  in_17,
  output [3:0] out_18,
  output out_19,
  output out_20,
  output out_21,
  output out_22,
  output out_23,
  output [7:0] out_24,
  output [31:0] out_25,
  output [7:0] out_26,
  output [7:0] out_27,
  output [15:0] out_28
);

  wire clock_1_out, clock_2_out, clock_3_out, clock_4_out, clock_5_out, d_ff_2_q, decoder_1_out0,
       decoder_1_out1, not_1_out, not_2_out, s_r_ff_2_q, xnor_1_out, xor_1_out;

  Clock clock_1 (.out(clock_1_out));
  Divider divider_1 (.a(in_9), .b(in_10), .out(out_24), .upper(in_8), .rem(out_26));
  assign out_28 = {{8{1'b0}}, in_16};  // Bit_Extender bit_extender_1
  S_R_Flip_Flop s_r_ff_1 ();  // open: S, clk, R, Q, Qn, preset, reset, en
  J_K_Flip_Flop j_k_ff_1 (.clk(clock_1_out));  // open: J, K, Q, Qn, preset, en, reset
  Multiplier #(.width(2)) multiplier_1 (
    .a(in_2[1:0]), .b(in_2[3:2]), .out(out_18[1:0]), .cin(in_1), .cout(out_18[3:2]));
  Clock clock_2 (.out(clock_2_out));
  xnor xnor_1 (xnor_1_out, s_r_ff_2_q, clock_2_out);
  not not_1 (not_1_out, xor_1_out);
  S_R_Flip_Flop s_r_ff_2 (
    .S(xnor_1_out), .clk(clock_2_out), .R(clock_2_out), .Q(s_r_ff_2_q), .en(in_5));  // open: Qn, preset, reset
  xor xor_1 (xor_1_out, out_23, clock_2_out);
  Decoder #(.enable("false")) decoder_1 (.out0(decoder_1_out0), .out1(decoder_1_out1), .sel(in_17));
  D_Flip_Flop d_ff_1 (.clk(clock_2_out), .D(not_1_out), .Q(out_23));  // open: Qn, preset, en, reset
  RAM #(.bus("separate")) ram_1 (
    .addr(in_12), .din(in_15), .data(out_27), .str(decoder_1_out0), .clk(clock_3_out), .ld(decoder_1_out1));  // open: sel, clr
  Clock clock_3 (.out(clock_3_out));
  Clock clock_4 (.out(clock_4_out));
  Clock clock_5 (.out(clock_5_out));
  not not_2 (not_2_out, d_ff_2_q);
  Demultiplexer #(.select(2), .enable("false")) demultiplexer_1 (
    .out0(out_19), .out1(out_20), .out2(out_21), .out3(out_22), .in(in_3), .sel(in_4));
  byteRam byteram_1 (
    .mode_0_byte_1_word(in_13), .D(in_6), .A(in_11), .store(in_14), .Clock(clock_5_out), .\output (out_25));
  D_Flip_Flop d_ff_2 (.clk(clock_4_out), .D(not_2_out), .Q(d_ff_2_q));  // open: Qn, preset, en, reset
endmodule

module byteRam (
  input  mode_0_byte_1_word,
  input  [31:0] D,
  input  [25:0] A,
  input  store,
  input  Clock,
  output [31:0] \output 
);

  wire [1:0] bitselector_1_out;
  wire [4:0] bit_extender_1_out, shifter_2_out;
  wire [7:0] bitselector_2_out, multiplexer_2_out;
  wire [23:0] bitselector_3_out;
  wire [25:0] shifter_1_out;
  wire [31:0] bit_extender_2_out, bit_extender_3_out, multiplexer_1_out, or_1_out, ram_1_data, shifter_3_out;

  BitSelector #(.width(26), .group(2)) bitselector_1 (.in(A), .out(bitselector_1_out), .sel(4'b0000));
  BitSelector #(.width(32), .group(8)) bitselector_2 (.in(D), .out(bitselector_2_out), .sel(2'b00));
  Shifter #(.width(26), .shift("lr")) shifter_1 (.in(A), .\dist (5'b00010), .out(shifter_1_out));
  assign bit_extender_1_out = {{3{1'b0}}, bitselector_1_out};  // Bit_Extender bit_extender_1
  BitSelector #(.width(26), .group(24)) bitselector_3 (.in(shifter_1_out), .out(bitselector_3_out), .sel(1'b0));
  Multiplexer #(.width(32), .enable("false")) multiplexer_1 (
    .in0(or_1_out), .in1(D), .out(multiplexer_1_out), .sel(mode_0_byte_1_word));
  assign bit_extender_2_out = {{24{1'b0}}, bitselector_2_out};  // Bit_Extender bit_extender_2
  Shifter #(.width(5)) shifter_2 (.in(bit_extender_1_out), .\dist (3'b011), .out(shifter_2_out));
  Shifter #(.width(32)) shifter_3 (.in(bit_extender_2_out), .\dist (shifter_2_out), .out(shifter_3_out));
  RAM #(.addrWidth(24), .dataWidth(32), .bus("separate")) ram_1 (
    .addr(bitselector_3_out), .din(multiplexer_1_out), .data(ram_1_data), .str(store), .clk(Clock), .ld(1'b1));  // open: sel, clr
  assign or_1_out = shifter_3_out | ram_1_data;  // OR_Gate or_1, 32 bits wide
  Multiplexer #(.select(2), .width(8), .enable("false")) multiplexer_2 (
    .in0(ram_1_data[7:0]), .in1(ram_1_data[15:8]), .in2(ram_1_data[23:16]), .in3(ram_1_data[31:24]),
    .out(multiplexer_2_out), .sel(bitselector_1_out));
  assign bit_extender_3_out = {{24{1'b0}}, multiplexer_2_out};  // Bit_Extender bit_extender_3
  Multiplexer #(.width(32), .enable("false")) multiplexer_3 (
    .in0(bit_extender_3_out), .in1(ram_1_data), .out(\output ), .sel(mode_0_byte_1_word));
endmodule

module subcontroller (
  input  a,
  input  b,
  input  c,
  input  d,
  output jump,
  output link,
  output \byte ,
  output memread,
  output memwrite,
  output regWrite,
  output immflag,
  output branch,
  output branchcomparator
);

  wire and_3_out, and_4_out, and_5_out, and_6_out, and_7_out, and_8_out, and_9_out, and_10_out, and_11_out,
       and_12_out, and_13_out, and_14_out, and_15_out, and_16_out, and_17_out, and_18_out, and_19_out,
       and_20_out, not_1_out, not_2_out, not_3_out, not_4_out, not_5_out, not_6_out, not_7_out, not_8_out,
       not_9_out, not_10_out, not_11_out, not_12_out, not_13_out, not_14_out, not_15_out, not_16_out,
       not_17_out, not_18_out;

  and and_1 (jump, b, c);
  and and_2 (link, b, c, d);
  not not_1 (not_1_out, c);
  or or_1 (\byte , not_1_out, b);
  not not_2 (not_2_out, b);
  and and_3 (and_3_out, not_2_out, c);
  and and_4 (and_4_out, b, not_3_out);
  not not_3 (not_3_out, c);
  and and_5 (and_5_out, a, d);
  and and_6 (and_6_out, a, b);
  not not_4 (not_4_out, b);
  and and_7 (and_7_out, not_4_out, c, d);
  not not_5 (not_5_out, c);
  and and_8 (and_8_out, b, not_5_out, d);
  and and_9 (and_9_out, a, c);
  and and_10 (and_10_out, a, b);
  not not_6 (not_6_out, a);
  and and_11 (and_11_out, not_6_out, not_7_out, not_8_out);
  not not_7 (not_7_out, b);
  not not_8 (not_8_out, c);
  not not_9 (not_9_out, a);
  and and_12 (and_12_out, not_9_out, not_10_out, not_11_out);
  not not_10 (not_10_out, b);
  not not_11 (not_11_out, d);
  not not_12 (not_12_out, a);
  and and_13 (and_13_out, not_12_out, not_13_out, not_14_out);
  not not_13 (not_13_out, c);
  not not_14 (not_14_out, d);
  and and_14 (and_14_out, b, c, d);
  and and_15 (and_15_out, a, c);
  and and_16 (and_16_out, a, b);
  not not_15 (not_15_out, b);
  and and_17 (and_17_out, not_15_out, d);
  not not_16 (not_16_out, b);
  and and_18 (and_18_out, not_16_out, c);
  and and_19 (and_19_out, b, not_17_out);
  not not_17 (not_17_out, c);
  and and_20 (and_20_out, a, b);
  not not_18 (not_18_out, d);
  or or_2 (branchcomparator, not_18_out, b);
  or or_3 (memread, and_3_out, and_4_out, and_5_out, and_6_out);
  or or_4 (memwrite, and_7_out, and_8_out, and_9_out, and_10_out);
  or or_5 (immflag, and_17_out, and_18_out, and_19_out, and_20_out);
  or or_6 (regWrite, and_11_out, and_12_out, and_13_out, and_14_out, and_15_out, and_16_out);

  assign branch = a;
endmodule

module regDecoder (
  input  [31:0] instruction,
  output [3:0] regDest,
  output [3:0] reg2,
  output [3:0] reg1
);


  assign reg1 = instruction[19:16];
  assign reg2 = instruction[15:12];
  assign regDest = instruction[23:20];
endmodule

module ALUmuxDec (
  input  B0,
  input  B1,
  input  B2,
  input  B4,
  output Y0,
  output Y1
);

  wire and_1_out, and_2_out, not_1_out, not_2_out;

  not not_1 (not_1_out, B0);
  and and_1 (and_1_out, not_1_out, B1);
  and and_2 (and_2_out, B1, B2);
  and and_3 (Y1, B0, B1, not_2_out);
  not not_2 (not_2_out, B4);
  or or_1 (Y0, and_1_out, and_2_out);
endmodule
